# Fritzing sketch christmas_tunes (saved by Fritzing 0.7.10b)
breadboards: 1

parts:
  Arduino1 = Arduino
  R1 = Resistor [tolerance=±5% resistance=220 package=THT]
  S1 = Pushbutton [package=THT]
  J1 = Piezo Speaker
  LED2 = LED - 5mm [color="Red (633nm)" package="5 mm [THT]"]
  LED3 = LED - 5mm [color="Red (633nm)" package="5 mm [THT]"]
  LED4 = LED - 5mm [color="Red (633nm)" package="5 mm [THT]"]
  LED5 = LED - 5mm [color="Red (633nm)" package="5 mm [THT]"]
  R3 = Resistor [tolerance=±5% resistance=220 package=THT]
  R4 = Resistor [tolerance=±5% resistance=220 package=THT]
  R2 = Resistor [tolerance=±5% resistance=220 package=THT]
  LED1 = LED - 5mm [color="Red (633nm)" package="5 mm [THT]"]
  R5 = Resistor [tolerance=±5% resistance=220 package=THT]
  R6 = Resistor [tolerance=±5% resistance=220 package=THT]

nets (from the schematic view):
  N1: Arduino1.GND, R1.Pin_1, J1.pin2, LED2.cathode, LED3.cathode, LED4.cathode, LED5.cathode, LED1.cathode
  N2: Arduino1.D8, J1.pin1
  N3: Arduino1.D7, R6.Pin_1
  N4: Arduino1.D6, R5.Pin_1
  N5: Arduino1.D5, R4.Pin_1
  N6: Arduino1.D4, R3.Pin_1
  N7: Arduino1.D3, R2.Pin_1
  N8: Arduino1.D2, R1.Pin_0, S1.leg0
  N9: Arduino1.+5V, S1.leg1
  N10: LED2.anode, R3.Pin_0
  N11: LED3.anode, R4.Pin_0
  N12: LED4.anode, R5.Pin_0
  N13: LED5.anode, R6.Pin_0
  N14: R2.Pin_0, LED1.anode
